# Fritzing sketch wire-layout (saved by Fritzing 0.9.4)
perfboards: 1

parts:
  Capacitive_Soil_Moisture_Sensor1 = DFRobot Capacitive Soil Moisture Sensor V1.0 [part_number=SEN0193]
  OLED1 = SSD1306 0.96in 128x64 I2C Monochrome OLED Display
  NodeMCU_v1 = NodeMCU v3 LoLin [part_number=ESP8266]
  S1 = Pushbutton [package="[THT]"]  # not connected
  R1 = Resistor [tolerance=±5% resistance=10k package="2512 [SMD]"]
  J1 = female pin header, 15 pins [form="♀ (female)"]
  J2 = female pin header, 15 pins [form="♀ (female)"]
  J3 = female pin header, 4 pins [form="♀ (female)"]
  J4 = female pin header, 3 pins [form="♀ (female)"]
  J5 = female pin header, 2 pins [form="♀ (female)"]
  M1 = DC Motor

nets:
  N1: Capacitive_Soil_Moisture_Sensor1.A, NodeMCU_v1.A0, J2.pin1, J4.pin3
  VCC: Capacitive_Soil_Moisture_Sensor1.VCC, OLED1.VCC, NodeMCU_v1.3V3, J1.pin6, J3.pin3, J4.pin2
  GND: Capacitive_Soil_Moisture_Sensor1.GND, OLED1.GND, NodeMCU_v1.GND, J2.pin2, J3.pin4, J4.pin1
  N2: OLED1.SCL, NodeMCU_v1.D2, J1.pin3, J3.pin1
  N3: OLED1.SDA, J3.pin2
  N4: NodeMCU_v1.D1, J1.pin2
  N5: R1.Pin_1, J1.pin14
  N6: J5.pin1, M1.pin_1
  N7: J5.pin2, M1.pin_2

custom parts:
  DFRobot Capacitive Soil Moisture Sensor V1.0: DFRobot Capacitive Soil Moisture Sensor V1.0 This product measures soil moisture levels by capacitive sensing, rather than resistive sensing like other types of moisture sensor. It is made of a corrosion resistant material giving it a long service life. Insert it into soil and impress your friends with the real-time soil moisture data! The product includes an on-board voltage regulator which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
  NodeMCU v3 LoLin: NodeMCU v3 LoLin NodeMCU (http://www.nodemcu.com/) is an open source IoT platform. It includes firmware (https://nodemcu-build.com/) which runs on the ESP8266 Wi-Fi SoC from Espressif Systems, and hardware which is based on the ESP-12E module. The term "NodeMCU" by default refers to the firmware rather than the dev kits. The firmware uses the Lua scripting language. It is based on the eLua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
